// Logisim project Circuit 1.circ as structural Verilog: 1 circuit, main circuit main
module main (
  input  A,
  input  B
);

  wire nand_1_out, not_1_out, not_2_out, xor_1_out;

  not not_1 (not_1_out, A);
  not not_2 (not_2_out, B);
  xor xor_1 (xor_1_out, not_1_out, B);
  nand nand_1 (nand_1_out, A, not_2_out);
  // OR_Gate or_1 has open pins: in0=xor_1_out, in1=nand_1_out, out=open
endmodule
