// Logisim project Circuit 2.circ as structural Verilog: 1 circuit, main circuit main
module main (
  input  A,
  input  B,
  input  C
);

  wire and_1_out, and_2_out, not_1_out;

  not not_1 (not_1_out, A);
  and and_1 (and_1_out, B, C);
  and and_2 (and_2_out, not_1_out, and_1_out);
  // OR_Gate or_1 has open pins: in0=not_1_out, in1=and_2_out, out=open
endmodule
