// Logisim project Circuit 3.circ as structural Verilog: 1 circuit, main circuit main
module main (
  input  A,
  input  B
);

  wire and_1_out, not_1_out, not_2_out;

  not not_1 (not_1_out, B);
  not not_2 (not_2_out, A);
  and and_1 (and_1_out, A, not_1_out);
  // NAND_Gate nand_1 has open pins: in0=not_2_out, in1=and_1_out, out=open
endmodule
