// Logisim project Circuit 4.circ as structural Verilog: 1 circuit, main circuit main
module main (
  input  A,
  input  B,
  input  C,
  input  D
);

  wire or_1_out, or_2_out;

  or or_1 (or_1_out, A, B);
  or or_2 (or_2_out, C, D);
  // XOR_Gate xor_1 has open pins: in0=or_1_out, in1=or_2_out, out=open
endmodule
