// Logisim project Circuit 1.circ as structural Verilog: 1 circuit, main circuit main
module main (
  input  A,
  input  B,
  output X
);

  wire nand_1_out, not_1_out, not_2_out, xor_1_out;

  not not_1 (not_1_out, A);
  not not_2 (not_2_out, B);
  xor xor_1 (xor_1_out, not_1_out, B);
  nand nand_1 (nand_1_out, A, not_2_out);
  and and_1 (X, xor_1_out, nand_1_out);

  // Notes on the sheet:
  //   G0
  //   W0
  //   G2
  //   G1
  //   W1
  //   W2
  //   G3
  //   W3
  //   G4
endmodule
