// Logisim project Circuit 2.circ as structural Verilog: 1 circuit, main circuit main
module main (
  input  A,
  input  B,
  input  C,
  output X
);

  wire and_1_out, and_2_out, not_1_out;

  not not_1 (not_1_out, A);
  and and_1 (and_1_out, B, C);
  and and_2 (and_2_out, not_1_out, and_1_out);
  and and_3 (X, not_1_out, and_2_out);

  // Notes on the sheet:
  //   G0
  //   W0
  //   G1
  //   W1
  //   W2
  //   G2
  //   G3
endmodule
