// Logisim project Circuit 3.circ as structural Verilog: 1 circuit, main circuit main
module main (
  input  A,
  input  B,
  output X
);

  wire and_1_out, not_1_out, not_2_out;

  not not_1 (not_1_out, B);
  not not_2 (not_2_out, A);
  and and_1 (and_1_out, A, not_1_out);
  nand nand_1 (X, not_2_out, and_1_out);

  // Notes on the sheet:
  //   G1
  //   W1
  //   G2
  //   G0
  //   W2
  //   W0
  //   G3
endmodule
