// Logisim project Circuit 4.circ as structural Verilog: 1 circuit, main circuit main
module main (
  input  A,
  input  B,
  input  C,
  input  D,
  output X
);

  wire or_1_out, or_2_out;

  or or_1 (or_1_out, A, B);
  or or_2 (or_2_out, C, D);
  xor xor_1 (X, or_1_out, or_2_out);

  // Notes on the sheet:
  //   G0
  //   G1
  //   W0
  //   W1
  //   G2
endmodule
